# Fritzing sketch HeadMouse (saved by Fritzing 0.9.4)
breadboards: 1

parts:
  Part1 = Arduino Mega 2560 (Rev3)
  Part2 = InvenSense MPU6050
  PmodBT1 = PmodBT2
  R1 = Resistor [tolerance=±5% resistance=1k package=THT]
  R2 = Resistor [tolerance=±5% resistance=2k package=THT]
  S1 = Round Pushbutton
  S2 = Round Pushbutton
  S3 = Round Pushbutton
  S4 = Round Pushbutton
  PmodBT3 = PmodBT2
  PmodBT4 = PmodBT2
  R3 = Resistor [tolerance=±5% resistance=1k package=THT]
  R4 = Resistor [tolerance=±5% resistance=2k package=THT]
  R5 = Resistor [tolerance=±5% resistance=2k package=THT]
  R6 = Resistor [tolerance=±5% resistance=1k package=THT]

nets:
  N1: Part1.D21/SCL, Part2.SCL
  N2: Part1.D20/SDA, Part1.SDA, Part2.SDA
  N3: Part1.D19/RX1, PmodBT1.NC#8
  N4: Part1.D18/TX1, R1.Pin_0
  N5: Part1.D17_PWM/RX2, PmodBT4.NC
  N6: Part1.D16_PWM/TX2, R3.Pin_0
  N7: Part1.D15/RX3, PmodBT3.NC
  N8: Part1.D14/TX3, R6.Pin_0
  GND: Part1.GND, Part2.GND, PmodBT1.NC#9, PmodBT1.GND, R2.Pin_1, S1.leg1, S2.leg1, S3.leg1, S4.leg0, PmodBT3.GND, PmodBT4.GND, R4.Pin_1, R5.Pin_1
  VCC: Part1.3V3, PmodBT1.VCC, PmodBT3.VCC, PmodBT4.VCC
  N9: Part1.D2_PWM, S1.leg0
  N10: Part1.D3_PWM, S2.leg0
  N11: Part1.D4_PWM, S3.leg0
  N12: Part1.D5_PWM, S4.leg1
  5V: Part1.5V, Part2.VCC
  N13: PmodBT1.STATUS, PmodBT1.RST, R1.Pin_1, R2.Pin_0
  N14: PmodBT3.RST, R5.Pin_0, R6.Pin_1
  N15: PmodBT4.STATUS, PmodBT4.RST, R3.Pin_1, R4.Pin_0

custom parts:
  PmodBT2: The PmodBT2 is a powerful peripheral module employing the Roving Networks® RN-42 to create a fully integrated Bluetooth interface. The PmodBT2 uses a standard 12-pin connection and communicates via UART. There is a secondary SPI header on the board for updating the RN-42 firmware if needed.
